// Logisim project Alphabets-In-Braille.circ as structural Verilog: 1 circuit, main circuit main
module main (
  output out_1,
  output out_2,
  output out_3,
  output out_4,
  output out_5,
  output out_6
);

  wire and_1_out, and_2_out, and_3_out, and_4_out, and_5_out, and_6_out, and_7_out, and_8_out, and_9_out,
       and_10_out, and_11_out, and_12_out, and_13_out, and_14_out, and_15_out, and_16_out, and_17_out,
       clock_1_out, not_1_out, not_2_out, not_3_out, not_4_out, not_5_out, not_6_out, not_7_out, not_8_out,
       not_9_out, not_10_out, not_11_out, not_12_out, not_13_out, not_14_out, not_15_out, not_16_out,
       not_17_out, not_18_out, not_19_out, not_20_out, or_1_out, or_2_out, or_3_out, or_4_out, or_5_out,
       or_6_out, xor_1_out;

  not not_1 (not_1_out, out_1);
  not not_2 (not_2_out, out_2);
  not not_3 (not_3_out, out_6);
  not not_4 (not_4_out, out_2);
  not not_5 (not_5_out, out_1);
  not not_6 (not_6_out, out_2);
  not not_7 (not_7_out, out_3);
  not not_8 (not_8_out, out_4);
  not not_9 (not_9_out, out_2);
  not not_10 (not_10_out, out_4);
  not not_11 (not_11_out, out_6);
  not not_12 (not_12_out, out_2);
  not not_13 (not_13_out, out_3);
  not not_14 (not_14_out, out_6);
  not not_15 (not_15_out, out_1);
  not not_16 (not_16_out, out_1);
  not not_17 (not_17_out, out_5);
  not not_18 (not_18_out, out_2);
  not not_19 (not_19_out, out_2);
  not not_20 (not_20_out, out_1);
  and and_1 (and_1_out, not_1_out, out_4);
  and and_2 (and_2_out, out_3, out_6);
  and and_3 (and_3_out, not_2_out, out_3, out_4);
  and and_4 (and_4_out, out_4, not_3_out);
  and and_5 (and_5_out, not_4_out, out_3);
  and and_6 (and_6_out, out_1, out_2, out_4);
  and and_7 (and_7_out, not_5_out, out_4);
  and and_8 (and_8_out, not_6_out, not_7_out, not_8_out);
  and and_9 (and_9_out, not_9_out, not_10_out, not_11_out);
  and and_10 (and_10_out, not_12_out, not_13_out, not_14_out);
  and and_11 (and_11_out, not_15_out, out_4);
  xor xor_1 (xor_1_out, out_2, out_4);
  and and_12 (and_12_out, out_3, out_6);
  and and_13 (and_13_out, not_16_out, out_4, not_17_out);
  and and_14 (and_14_out, not_18_out, out_4, out_6);
  and and_15 (and_15_out, out_3, out_6);
  and and_16 (and_16_out, not_19_out, out_4, out_6);
  and and_17 (and_17_out, not_20_out, out_4, out_5);
  or or_1 (or_1_out, and_1_out, and_2_out, and_3_out);
  or or_2 (or_2_out, and_4_out, and_5_out, and_6_out);
  or or_3 (or_3_out, and_7_out, and_8_out, and_9_out, and_10_out);
  or or_4 (or_4_out, and_11_out, xor_1_out, and_12_out);
  or or_5 (or_5_out, and_13_out, and_14_out, and_15_out);
  or or_6 (or_6_out, and_16_out, and_17_out);
  Clock clock_1 (.out(clock_1_out));
  T_Flip_Flop t_ff_1 (.clk(clock_1_out), .T(or_1_out), .Q(out_1));  // open: Qn, preset, reset, en
  T_Flip_Flop t_ff_2 (.clk(clock_1_out), .T(or_2_out), .Q(out_2));  // open: Qn, preset, reset, en
  T_Flip_Flop t_ff_3 (.clk(clock_1_out), .T(or_3_out), .Q(out_3));  // open: Qn, preset, reset, en
  T_Flip_Flop t_ff_4 (.clk(clock_1_out), .T(or_4_out), .Q(out_4));  // open: Qn, preset, reset, en
  T_Flip_Flop t_ff_5 (.clk(clock_1_out), .T(or_5_out), .Q(out_5));  // open: Qn, preset, reset, en
  T_Flip_Flop t_ff_6 (.clk(clock_1_out), .T(or_6_out), .Q(out_6));  // open: Qn, preset, reset, en

  // Notes on the sheet:
  //   A B C D E F
  //   A
  //   B
  //   C
  //   D
  //   E
  //   F
  //   Alphabets
  //   In
  //   Braille
  //   Script
endmodule
