// Logisim project BCD-to-Braille.circ as structural Verilog: 1 circuit, main circuit main
module main (
  input  [3:0] W_X_Y_Z,
  input  in_2,
  input  in_3,
  output A,
  output B,
  output out_6,
  output C,
  output out_8,
  output out_9,
  output D,
  output F,
  output out_12,
  output E,
  output out_14,
  output out_15
);

  wire and_1_out, and_2_out, and_3_out, and_4_out, and_5_out, and_6_out, and_7_out, and_8_out, not_1_out,
       not_2_out, not_3_out, not_4_out, not_5_out, not_6_out, not_7_out, xor_1_out;

  not not_1 (not_1_out, W_X_Y_Z[2]);
  and and_1 (and_1_out, not_1_out, not_2_out);
  not not_2 (not_2_out, W_X_Y_Z[0]);
  and and_2 (and_2_out, W_X_Y_Z[1], W_X_Y_Z[2]);
  xor xor_1 (xor_1_out, W_X_Y_Z[0], W_X_Y_Z[3]);
  or or_1 (A, W_X_Y_Z[1], W_X_Y_Z[2], xor_1_out);
  or or_2 (D, and_1_out, and_2_out, W_X_Y_Z[3]);
  not not_3 (not_3_out, W_X_Y_Z[0]);
  not not_4 (not_4_out, W_X_Y_Z[1]);
  not not_5 (not_5_out, W_X_Y_Z[1]);
  not not_6 (not_6_out, W_X_Y_Z[0]);
  not not_7 (not_7_out, W_X_Y_Z[3]);
  and and_3 (and_3_out, W_X_Y_Z[0], W_X_Y_Z[2]);
  and and_4 (and_4_out, not_3_out, not_4_out);
  and and_5 (and_5_out, not_5_out, not_6_out, not_7_out);
  and and_6 (and_6_out, W_X_Y_Z[0], W_X_Y_Z[1]);
  and and_7 (and_7_out, W_X_Y_Z[0], W_X_Y_Z[3]);
  and and_8 (and_8_out, W_X_Y_Z[1], W_X_Y_Z[2]);
  or or_3 (F, and_3_out, and_4_out);
  or or_4 (B, and_5_out, and_6_out, and_7_out, and_8_out);
  not not_8 (out_6, 1'b1);
  not not_9 (out_8, 1'b1);

  assign C = 1'b1;
  assign E = 1'b1;
  assign out_9 = 1'b1;
  assign out_12 = 1'b1;
  assign out_14 = in_2;
  assign out_15 = in_3;

  // Notes on the sheet:
  //   BCD number
  //   A
  //   c
  //   BCD NUMBER TO BRAILLE NUMBER CONVERTER
  //   B
  //   D
  //   0 to 9
endmodule
